# Fritzing sketch LozaSaber (saved by Fritzing 0.9.3b)

parts:
  Part1 = Arduino Nano (Rev3.0)
  U2 = BATTERY-2 [package=battery-aa]
  CS_|_SCK_|_MOSI_|_MISO_|_VCC_|_GND = MicroSD Card Module
  GY1 = MPU-6050 Board GY-521 [form="♀ (female)" package=THT]
  U3 = SBX DSUN [package=THT]
  M1 = PAM8403 Stereo Amplifier [part_number=HW-104]
  SP1 = SPEAKER [package=pcb_mount_speaker]
  S1 = Round Pushbutton
  U4 = SWITCH-SPST-2 [package=switch-spst-vertical]
  RGB_SMD_LED4 = SMD RGB LED (WS2812) [package=5050]
  J1 = Power Jack [package=power_jack_combo]
  R1 = Resistor [tolerance=±5% resistance=464 package=THT]
  R2 = Resistor [tolerance=±5% resistance=1k package=THT]
  R3 = Resistor [tolerance=±5% resistance=220 package=THT]

nets:
  GND: Part1.GND, CS_|_SCK_|_MOSI_|_MISO_|_VCC_|_GND.GND, GY1.pin2, U3.GND, M1.POWER-, M1.INPUTG, RGB_SMD_LED4.VSS
  N1: Part1.D3, S1.leg0
  N2: Part1.D6, R3.Pin_0
  N3: Part1.D8, CS_|_SCK_|_MOSI_|_MISO_|_VCC_|_GND.CS
  N4: Part1.D9, M1.INPUTL
  N5: Part1.D11/MOSI, CS_|_SCK_|_MOSI_|_MISO_|_VCC_|_GND.MOSI
  N6: Part1.D12/MISO, CS_|_SCK_|_MOSI_|_MISO_|_VCC_|_GND.MISO
  N7: Part1.VIN, U4.P, R2.Pin_1
  5V: Part1.5V, CS_|_SCK_|_MOSI_|_MISO_|_VCC_|_GND.VCC
  N8: Part1.A6, R1.Pin_1
  N9: Part1.A5, GY1.pin3
  N10: Part1.A4, GY1.pin4
  N11: Part1.3V3, GY1.pin1
  N12: Part1.D13/SCK, CS_|_SCK_|_MOSI_|_MISO_|_VCC_|_GND.SCK
  N13: U2.-1, J1.GNDBREAK
  N14: U2.+1, U4.O, J1.PWR
  N15: U3.+VOUT#4, RGB_SMD_LED4.VDD
  N16: U3.+VOUT#5, M1.POWER+
  N17: M1.LOUT+, SP1.-
  N18: M1.LOUT-, SP1.+
  N19: RGB_SMD_LED4.NC, R3.Pin_1

notes:
  5V

custom parts:
  MPU-6050 Board GY-521: Acelerometro y Giroscopio MPU-6050 Board GY-521
  SBX DSUN: SBX DSUN input voltage 4.5 - 28V DC output voltage .8v to 20VDC (step down converter) Output current 3A max
  PAM8403 Stereo Amplifier: PAM8403 stereo amplifier module Descriptive words Links: PAM8403 product datasheet
